// Logisim project ALU4_AND_OR_SLT.circ as structural Verilog: 1 circuit, main circuit ALU4
module ALU4 (
  input  [3:0] A,
  input  [3:0] B,
  input  [1:0] OP,
  output [3:0] Result
);

  wire and_2_out, D3, SLT, xor_1_out, xor_2_out;
  wire [2:0] subtractor_1_out;
  wire [3:0] AND_out, OR_out, SLT4;

  assign AND_out = A & B;  // AND_Gate and_1, 4 bits wide
  assign OR_out = A | B;  // OR_Gate or_1, 4 bits wide
  Subtractor #(.width(4)) subtractor_1 (.a(A), .b(B), .out({D3, subtractor_1_out}), .bin(1'b0));  // open: bout
  Multiplexer #(.select(2), .width(4), .enable("false")) multiplexer_1 (
    .in0(AND_out), .in1(OR_out), .in2(SLT4), .in3(4'b0000), .out(Result), .sel(OP));
  xor xor_1 (xor_1_out, A[3], B[3]);
  xor xor_2 (xor_2_out, A[3], D3);
  and and_2 (and_2_out, xor_1_out, xor_2_out);
  xor xor_3 (SLT, and_2_out, D3);
  assign SLT4 = {{3{1'b0}}, SLT};  // Bit_Extender bit_extender_1

  // Notes on the sheet:
  //   Bitwise AND
  //   Bitwise OR
  //   SLT stage 1: D = A - B
  //   D3 = sign bit of D
  //   Extract MSBs (sign bits)
  //   4-bit ALU : AND / OR / SLT  (operation selected by a 4:1 multiplexer)
  //   OP = 00 -> A AND B    01 -> A OR B    10 -> SLT (A<B signed)    11 -> 0000
  //   4:1 MUX (4 bits wide), select = OP
  //   in0=AND  in1=OR  in2=SLT  in3=0
  //   SLT stage 2: V = (A3 xor B3) and (A3 xor D3);  SLT = D3 xor V
  //   V = overflow
  //   Zero-extend: 000S
endmodule
