// Logisim project PROJECT 2.circ as structural Verilog: 1 circuit, main circuit main
module main (
  input  A,
  input  B,
  input  A_2,
  input  B_2,
  input  Cin,
  input  in_6,
  input  in_7,
  output SUM,
  output CARRY,
  output S,
  output Cout
);

  wire and_2_out, and_3_out, undriven, xor_2_out;

  xor xor_1 (SUM, B, A);
  and and_1 (CARRY, B, A);
  ExactlyOne xor_2 (.out(xor_2_out), .in0(A_2), .in3(B_2), .in4(B_2));
  and and_2 (and_2_out, B_2, A_2);
  Adder #(.width(1)) adder_1 (.a(in_6), .b(in_7), .cin(undriven));  // open: out, cout
  and and_3 (and_3_out, xor_2_out, Cin);
  xor xor_3 (S, xor_2_out, Cin);
  or or_1 (Cout, and_3_out, and_2_out);
  Multiplexer multiplexer_1 ();  // open: in0, in1, out, sel, en
endmodule
